# Fritzing sketch analog_in (saved by Fritzing 0.7.0b)
breadboards: 1

parts:
  U1 = Arduino Mega
  R1 = Rotary Potentiometer (Small) [maximum_resistance=100kΩ]

nets:
  N1: U1.GND, R1.leg1
  N2: U1.+5V, R1.leg2
  N3: U1.A0, R1.wiper
