# Fritzing sketch analog_out (saved by Fritzing 0.7.0b)
breadboards: 1

parts:
  U1 = Arduino Mega
  LED1 = LED - 5mm [color="Red (633nm)" package="5 mm [THT]"]
  R1 = Resistor [tolerance=±5% resistance=220 package=THT]

nets:
  N1: U1.GND, LED1.cathode
  N2: U1.D2, R1.Pin_1
  N3: LED1.anode, R1.Pin_0
