# Fritzing sketch digital_in (saved by Fritzing 0.7.0b)
breadboards: 1

parts:
  U1 = Arduino Mega
  S1 = Pushbutton [package="[THT]"]

nets:
  N1: U1.GND, S1.Pin_1, S1.Pin_2
  N2: U1.A0, S1.Pin_3, S1.Pin_4
