# Fritzing sketch fff (saved by Fritzing 0.7.0b)
breadboards: 1

parts:
  U1 = Arduino Mega
  S2 = Pushbutton [package="[THT]"]
  S3 = Pushbutton [package="[THT]"]
  S4 = Pushbutton [package="[THT]"]
  S5 = Pushbutton [package="[THT]"]

nets:
  N1: U1.GND, S2.Pin_3, S2.Pin_4, S3.Pin_3, S3.Pin_4, S4.Pin_3, S4.Pin_4, S5.Pin_3, S5.Pin_4
  N2: U1.D9, S5.Pin_1, S5.Pin_2
  N3: U1.D8, S4.Pin_1, S4.Pin_2
  N4: U1.D7, S3.Pin_1, S3.Pin_2
  N5: U1.D6, S2.Pin_1, S2.Pin_2
