# Fritzing sketch adk_basic_full (saved by Fritzing 0.7.0b)
breadboards: 1

parts:
  R1 = Resistor [tolerance=±5% resistance=220 package=THT]
  LED1 = LED - 5mm [color="Red (633nm)" package="5 mm [THT]"]
  S1 = Pushbutton [package="[THT]"]
  U1 = Arduino Mega
  R6 = Rotary Potentiometer (Small) [maximum_resistance=100kΩ]
  LED4 = LED - 5mm [color="Green (570nm)" package="5 mm [THT]"]
  LED5 = LED - 5mm [color="Red (633nm)" package="5 mm [THT]"]
  LED6 = LED - 5mm [color="Red (633nm)" package="5 mm [THT]"]
  LED7 = LED - 5mm [color="Red (633nm)" package="5 mm [THT]"]
  R13 = Resistor [tolerance=±5% resistance=220 package=THT]
  R14 = Resistor [tolerance=±5% resistance=220 package=THT]
  R15 = Resistor [tolerance=±5% resistance=220 package=THT]
  R16 = Resistor [tolerance=±5% resistance=220 package=THT]
  R17 = Resistor [tolerance=±5% resistance=220 package=THT]
  R18 = Resistor [tolerance=±5% resistance=220 package=THT]
  R19 = Resistor [tolerance=±5% resistance=220 package=THT]
  LED8 = LED - 5mm [color="Green (570nm)" package="5 mm [THT]"]
  LED9 = LED - 5mm [color="Green (570nm)" package="5 mm [THT]"]
  LED10 = LED - 5mm [color="Green (570nm)" package="5 mm [THT]"]
  S3 = Pushbutton [package="[THT]"]
  S4 = Pushbutton [package="[THT]"]
  S5 = Pushbutton [package="[THT]"]
  R20 = Rotary Potentiometer (Small) [maximum_resistance=100kΩ]
  R21 = Rotary Potentiometer (Small) [maximum_resistance=100kΩ]
  R22 = Rotary Potentiometer (Small) [maximum_resistance=100kΩ]

nets:
  N1: R1.Pin_0, LED1.anode
  N2: R1.Pin_1, U1.D2
  N3: LED1.cathode, S1.Pin_3, S1.Pin_4, R6.leg1, LED4.cathode, LED5.cathode, LED6.cathode, LED7.cathode, LED8.cathode, LED9.cathode, LED10.cathode, S3.Pin_3, S3.Pin_4, S4.Pin_3, S4.Pin_4, S5.Pin_3, S5.Pin_4, R20.leg1, R21.leg1, R22.leg1
  N4: S1.Pin_1, S1.Pin_2, U1.D9
  N5: U1.D13, R17.Pin_1
  N6: U1.D12, R16.Pin_1
  N7: U1.D11, R19.Pin_1
  N8: U1.D10, R18.Pin_1
  N9: U1.D8, S4.Pin_1, S4.Pin_2
  N10: U1.D7, S3.Pin_1, S3.Pin_2
  N11: U1.D6, S5.Pin_1, S5.Pin_2
  N12: U1.D5, R14.Pin_1
  N13: U1.D4, R15.Pin_1
  N14: U1.+5V, R6.leg2, R20.leg2, R21.leg2, R22.leg2
  N15: U1.A0, R20.wiper
  N16: U1.A1, R6.wiper
  N17: U1.A2, R21.wiper
  N18: U1.A3, R22.wiper
  N19: LED4.anode, R18.Pin_0
  N20: LED5.anode, R14.Pin_0
  N21: LED6.anode, R15.Pin_0
  N22: LED7.anode, R13.Pin_0
  N23: R16.Pin_0, LED8.anode
  N24: R17.Pin_0, LED10.anode
  N25: R19.Pin_0, LED9.anode
