# Fritzing sketch concierge (saved by Fritzing 0.7.0b)
breadboards: 1

parts:
  U1 = Arduino Mega
  CONN1 = USB connector [package=THT]
  CONN2 = USB connector [package=THT]
  Q2 = NPN-Transistor [package="TO92 [THT]"]
  R1 = Resistor [tolerance=±5% resistance=220 package=THT]
  Q3 = NPN-Transistor [package="TO92 [THT]"]
  R2 = Resistor [tolerance=±5% resistance=220 package=THT]

nets:
  N1: U1.GND, Q2.C, Q3.C
  N2: U1.D3, R1.Pin_0
  N3: U1.D2, R2.Pin_0
  N4: U1.+5V, CONN1.d-, CONN2.d-
  N5: CONN1.GND, CONN1.chassis5, CONN1.chassis6, Q2.E
  N6: CONN2.GND, CONN2.chassis5, CONN2.chassis6, Q3.E
  N7: Q2.B, R1.Pin_1
  N8: Q3.B, R2.Pin_1
