# Fritzing sketch socialalarm (saved by Fritzing 0.7.0b)
breadboards: 1

parts:
  U1 = Arduino Mega
  Q1 = NPN-Transistor [package="TO92 [THT]"]
  M1 = DC Motor
  VCC1 = Battery
  S1 = Toggle Switch [package=THT]
  R1 = Resistor [tolerance=±5% resistance=220 package=THT]

nets:
  N1: U1.D2, R1.Pin_1
  N2: U1.GND, Q1.E, VCC1.-
  N3: Q1.B, M1.pin_1
  N4: Q1.C, R1.Pin_0
  N5: M1.pin_2, S1.L1
