# Fritzing sketch ir_learning (saved by Fritzing 0.7.0b)
breadboards: 1

parts:
  U1 = Arduino Mega
  U2 = mystery part, 3 pins [chip_label=? spacing=300mil]

nets:
  N1: U1.+5V, U2.pin3
  N2: U1.GND, U2.pin2
  N3: U1.A0, U2.pin1
