# Fritzing sketch ir_remote (saved by Fritzing 0.7.0b)
breadboards: 1

parts:
  U1 = Arduino Mega
  LED1 = LED - 5mm [color="Infrared (940nm)" package="5 mm [THT]"]

nets:
  N1: U1.D2, LED1.anode
  N2: U1.GND, LED1.cathode
