# Fritzing sketch temperaturelogger (saved by Fritzing 0.7.0b)
breadboards: 1

parts:
  U1 = Arduino Mega
  T1 = LM34 Temperature Sensor [package="TO92 [THT]"]

nets:
  N1: U1.+5V, T1.+Vs
  GND: U1.GND, T1.GND
  N2: U1.A0, T1.Vout
